# Fritzing sketch SchematicoFR (saved by Fritzing 0.9.3b)
breadboards: 1

parts:
  Componente1 = Arduino Due (Rev2b)
  Componente2 = Adafruit Bluefruit LE UART Friend [part_number="Adafruit #2479"]
  Componente3 = Adafruit AMG8833 8x8 GRID EYE

nets:
  N1: Componente1.D20/SDA3, Componente3.SDA
  N2: Componente1.D21/SCL3, Componente3.SCL
  VIN: Componente1.5V, Componente2.VIN, Componente3.VIN
  GND: Componente1.GND, Componente2.GND, Componente3.GND
  N3: Componente1.D9_PWM, Componente2.RXI
  N4: Componente1.D10_PWM/SS0, Componente2.TXO
  N5: Componente1.D11_PWM, Componente2.CTS
  N6: Componente1.D12_PWM, Componente2.MODE
  N7: Componente1.D6_PWM, Componente2.RTS

custom parts:
  Adafruit Bluefruit LE UART Friend: The Bluefruit LE UART Friend makes it easy to add Bluetooth Low Energy connectivity to anything with a hardware or software serial port. We even have nice hardware flow control so you won't have to think about losing data. Connect to your Arduino or other microcontroller or even just a standard FTDI cable for debugging and testing.
